# Fritzing sketch dht11-proto (saved by Fritzing 0.9.6b)
breadboards: 1

parts:
  Componente1 = Franzininho WiFi
  RHT1 = Humidity and Temperature Sensor RHT03
  R1 = Resistor [tolerance=±5% power=0.25 resistance=10k package=THT]

nets:
  N1: Componente1.15, RHT1.Data-signal, R1.Pin_1
  N2: Componente1.GND#19, RHT1.GND_2
  3V3: Componente1.3V3, RHT1.Vcc, R1.Pin_0

custom parts:
  Franzininho WiFi: Placa de desenvolvimento ESP32-S2
