# Fritzing sketch macropad-franzininho (saved by Fritzing 0.9.6b)

parts:
  Componente1 = Franzininho WiFi
  S2 = Tactile Switch Buttons - 12mm Square [package=tactile-pth-12mm]
  S3 = Tactile Switch Buttons - 12mm Square [package=tactile-pth-12mm]
  S4 = Tactile Switch Buttons - 12mm Square [package=tactile-pth-12mm]
  S5 = Tactile Switch Buttons - 12mm Square [package=tactile-pth-12mm]
  S6 = Tactile Switch Buttons - 12mm Square [package=tactile-pth-12mm]
  S7 = Tactile Switch Buttons - 12mm Square [package=tactile-pth-12mm]

nets:
  N1: Componente1.2, S2.1, S2.3
  N2: Componente1.3, S3.3
  N3: Componente1.4, S5.1, S5.3
  N4: Componente1.5, S4.1, S4.3
  N5: Componente1.6, S7.1, S7.3
  N6: Componente1.7, S6.3
  N7: Componente1.GND, S2.2, S6.2, S6.4
  N8: S3.2, S5.2, S5.4
  N9: S4.2, S4.4, S7.2

custom parts:
  Franzininho WiFi: Placa de desenvolvimento ESP32-S2
  Tactile Switch Buttons - 12mm Square: Medium-sized clicky momentary switches are standard input "buttons" on electronic projects. These work best in a PCB but can be used on a solderless breadboard as shown in this tutorial. The pins are normally open (disconnected) and when the button is pressed they are momentarily closed. They come in a pack of 10, they're pretty handy so you'll want to keep them around. You can find an EAGLE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
